# Fritzing sketch robot_scheme (saved by Fritzing 0.9.10b)
stripboards: 1

parts:
  Компонент3 = NRF24L01
  HC-SR04_Sensor_1 = HC-SR04 Ultrasonic Distance Sensor
  Mod1 = Arduino Sensor Shield v5.0
  M1 = gear-motor
  M2 = gear-motor
  Компонент4 = Arduino Motor Shield (Rev3)
  Mod2 = Arduino Sensor Shield v5.0
  S1 = Toggle Switch [package=THT]
  S2 = Toggle Switch [package=THT]
  J2 = Basic Servo
  BAT2 = Battery Holders [package=lipo-1100mAh]
  BAT3 = Battery Holders [package=lipo-1100mAh]
  BAT4 = Battery Holders [package=lipo-1100mAh]
  BAT5 = Battery Holders [package=lipo-1100mAh]
  BAT6 = Battery Holders [package=lipo-1100mAh]
  J3 = Basic Servo
  J1 = Basic Servo  # not connected

nets:
  N1: Компонент3.MOSI, Компонент3.VCC, Mod1.SD-D11, Mod1.11-S, Mod1.ParallelLCD-D11
  N2: Компонент3.CSN, Mod1.10-S, Mod1.ParallelLCD-D10
  N3: Компонент3.MISO, Mod1.12-S, Mod1.ParallelLCD-D12
  N4: Компонент3.SCK, Mod1.SD-D13, Mod1.13-S, Mod1.ParallelLCD-D13, Mod2.SD-D13, Mod2.13-S
  N5: Компонент3.CE, Mod1.9-S, Mod1.ParallelLCD-D9
  GND: Компонент3.GND, HC-SR04_Sensor_1.GND, Mod1.GND, Mod1.12-G, Mod1.8-G, Mod1.ParallelLCD-GND
  N6: HC-SR04_Sensor_1.VCC, Mod1.8-V, Mod1.ParallelLCD-VCC
  N7: HC-SR04_Sensor_1.TRIG, Mod1.8-S, Mod1.ParallelLCD-D8
  N8: HC-SR04_Sensor_1.ECHO, Mod1.URF01-A0, Mod1.A0-SIG
  N9: Mod1.A4-SIG, Mod2.A4-SIG, Mod2.IIC-SDA
  N10: Mod1.A5-SIG, Mod2.A5-SIG, Mod2.IIC-SCL
  N11: M1.pin_1, Компонент4.B+
  N12: M1.pin_2, Компонент4.B-
  N13: M2.pin_1, Компонент4.A+
  N14: M2.pin_2, Компонент4.A-
  N15: Компонент4.VMOT, S1.COM
  N16: Компонент4.GND, BAT2.-, BAT3.-, BAT4.-
  N17: S1.L1, BAT2.+, BAT3.+, BAT4.+
  N18: S2.L2, BAT5.+, BAT6.+
  GND_2: J2.gnd, J3.gnd
  VCC: J2.vcc, J3.vcc
